# Fritzing sketch fritzing (saved by Fritzing 0.9.3b)
breadboards: 2

parts:
  U1 = ESP32S-HiLetgo [part_number=ESP32S-HiLetgo]
  U2 = POT [package=pot_mammoth]
  U3 = POT [package=pot_mammoth]
  U4 = POT [package=pot_mammoth]
  S1 = Pushbutton [package="[SMD]"]
  S2 = Pushbutton [package="[SMD]"]
  LED1 = RGB LED (com. anode, rbg) [package="5 mm [THT]"]
  R1 = Resistor [tolerance=±5% resistance=220 package="2512 [SMD]"]
  R2 = Resistor [tolerance=±5% resistance=220 package="2512 [SMD]"]
  R3 = Resistor [tolerance=±5% resistance=220 package="2512 [SMD]"]
  R4 = Resistor [tolerance=±5% resistance=220 package="2512 [SMD]"]
  R5 = Resistor [tolerance=±5% resistance=220 package="2512 [SMD]"]

nets:
  N1: U1.GPIO34, U4.A
  N2: U1.GPIO32, U2.A
  N3: U1.GPIO33, U3.A
  N4: U1.GPIO25, R3.Pin_0
  N5: U1.GPIO26, R5.Pin_0
  N6: U1.GPIO27, R4.Pin_0
  N7: U1.GPIO14, S1.Pin_3, S1.Pin_4, R1.Pin_0
  N8: U1.GND, U2.S, U3.S, U4.S, R1.Pin_1, R2.Pin_1
  N9: U1.GPIO13, S2.Pin_3, S2.Pin_4, R2.Pin_0
  N10: U1.VIN, U2.E, U3.E, U4.E, S1.Pin_1, S1.Pin_2, S2.Pin_1, S2.Pin_2, LED1.blue_cathode
  N11: LED1.red_cathode, R4.Pin_1
  N12: LED1.common_anode, R5.Pin_1
  N13: LED1.green_cathode, R3.Pin_1

custom parts:
  ESP32S-HiLetgo: HiLetgo ESP-WROOM-32 ESP32 ESP-32S Development Board 2.4GHz Dual-Mode WiFi + Bluetooth Dual Cores Microcontroller The ESP32 integrated with Antenna switches, RF Balun, power amplifiers, low-noise amplifiers, filters, and management modules, and the entire solution occupies the least area of PCB. 2.4 GHz Wi-Fi plus Bluetooth dual-mode chip, with TSMC Ultra-low power consumption 40nm technology,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
